# Fritzing sketch UV_Timer (saved by Fritzing 0.7.11b)
breadboards: 1

parts:
  12v_1A = Power plug
  U1 = Voltage Regulator - 5V [package="TO220 [THT]"]
  5v = Screw terminal - 2 pins [package=THT]
  + = Pushbutton [package=THT]
  - = Pushbutton [package=THT]
  OK = Pushbutton [package=THT]
  J2 = female pin header, 3 pins [form="♀ (female)"]
  Safety = Pushbutton [package=THT]
  J3 = female pin header, 1 pin [form="♀ (female)"]
  J4 = female pin header, 1 pin [form="♀ (female)"]
  Q1 = NPN-Transistor [package="TO92 [THT]"]
  LED_12v = Screw terminal - 2 pins [package=THT]
  LCD1 = LCD screen
  J5 = female pin header, 9 pins [form="♀ (female)"]
  J6 = female pin header, 1 pin [form="♀ (female)"]
  R1 = Resistor [tolerance=±5% resistance=2.2k package=THT]

nets:
  GND: 12v_1A.GND, U1.GND, 5v.pin1, LED_12v.pin1, LCD1.VSS, LCD1.R/W, LCD1.LED-, R1.Pin_1
  N1: 12v_1A.VCC, U1.input_voltage, Q1.C
  N2: U1.output_voltage, 5v.pin2, +.leg1, -.leg1, OK.leg1, Safety.leg1, LCD1.VDD, LCD1.LED+
  N3: +.leg0, J2.pin1
  N4: -.leg0, J2.pin2
  N5: OK.leg0, J2.pin3
  N6: Safety.leg0, J3.pin1
  N7: J4.pin1, Q1.B
  N8: Q1.E, LED_12v.pin2
  N9: LCD1.V0, R1.Pin_0
  N10: LCD1.RS, J6.pin1
  N11: LCD1.E, J5.pin1
  N12: LCD1.DB0, J5.pin2
  N13: LCD1.DB1, J5.pin3
  N14: LCD1.DB2, J5.pin4
  N15: LCD1.DB3, J5.pin5
  N16: LCD1.DB4, J5.pin6
  N17: LCD1.DB5, J5.pin7
  N18: LCD1.DB6, J5.pin8
  N19: LCD1.DB7, J5.pin9

notes:
  UV_box - P.O. - r1
